# Fritzing sketch seatpm_perfboard_layout (saved by Fritzing 0.9.4)
perfboards: 4

parts:
  Part1 = BadgerStick
  LCD1 = LCD screen  # not connected
  S1 = Round Pushbutton  # not connected
  S2 = Round Pushbutton  # not connected
  S3 = Round Pushbutton  # not connected
  S4 = Round Pushbutton  # not connected
  R1 = Resistor [tolerance=±5% resistance=220 package="2010 [SMD]"]  # not connected
  R2 = Resistor [tolerance=±5% resistance=220 package="2010 [SMD]"]  # not connected
  S5 = Square Pushbutton  # not connected
  S6 = Square Pushbutton  # not connected
  M1 = DC Motor  # not connected
  Q1 = TRANSISTOR_NPN [package=to-92-ammo]  # not connected
  Q2 = TRANSISTOR_NPN [package=to-92-ammo]  # not connected
  R3 = Resistor [tolerance=±5% resistance=220 package="2010 [SMD]"]  # not connected
  R4 = Resistor [tolerance=±5% resistance=220 package="2010 [SMD]"]  # not connected
  C1 = Ceramic Capacitor [capacitance="100 nF" package="0603 [SMD, multilayer]"]  # not connected
  U1 = ADXL345 [package=lga14]  # not connected
  U2 = ADXL345 [package=lga14]  # not connected

nets:
  N1: Part1.2.6, Part1.3.6, Part1.0.7
  N2: Part1.3.0, Part1.1.0
  N3: Part1.3.1, Part1.0.6

notes:
  Confirm Button
  Back Button
  Increment Button
  Decrement Button
  Contrast Voltage Divider
  Emergency Stop Button 1
  Emergency Stop Button 2
  Rotary Encoder
  Goniometer

custom parts:
  BadgerStick: Interactive Badges These badges were designed as a soldering demo for the SparkFun booths at Maker Faire. They were designed to teach the basics of PTH soldering, as well as to provide users with an Arduino platform they could take home and hack. Please view the tutorial on hacking your badge for more information.
